# Fritzing sketch cds_led_circuit (saved by Fritzing 0.9.3b)
breadboards: 1

parts:
  R1 = Resistor [tolerance=±5% resistance=10k package=THT]
  R2 = Photocell (LDR) [package=THT]
  부품1 = Arduino Uno (Rev3)
  LED1 = LED - 5mm [color="Green (555nm)" package="5 mm [THT]"]
  R3 = Resistor [tolerance=±5% resistance=330 package=THT]

nets:
  N1: R1.Pin_0, R2.pin_1, 부품1.A0
  N2: R1.Pin_1, 부품1.5V
  N3: R2.pin_0, 부품1.GND, R3.Pin_0
  N4: 부품1.D13/SCK, LED1.anode
  N5: LED1.cathode, R3.Pin_1
