# Fritzing sketch lcd_circuit_start (saved by Fritzing 0.9.3b)
breadboards: 1

parts:
  부품1 = Arduino Uno (Rev3)
  LCD1 = LCD screen
  R1 = Rotary Potentiometer (Small) [maximum_resistance=100kΩ package=THT]

nets:
  5V: 부품1.5V, LCD1.VDD, LCD1.LED+, R1.leg1
  GND: 부품1.GND, LCD1.VSS, LCD1.R/W, LCD1.LED-, R1.leg2
  N1: LCD1.V0, R1.wiper
